# Fritzing sketch gnu-slash-mood (saved by Fritzing 0.9.3b)

parts:
  BeagleBone1 = BeagleBone Black
  LED1 = LED - 5mm [color="Red (633nm)" package="5 mm [THT]"]
  LED2 = LED - 5mm [color="Green (570nm)" package="5 mm [THT]"]
  LED3 = LED - 5mm [color="Blue (505nm)" package="5 mm [THT]"]

nets:
  N1: BeagleBone1.P9_2, LED2.anode
  N2: BeagleBone1.P9_14, LED2.cathode
  N3: BeagleBone1.P8_1, LED3.cathode
  N4: BeagleBone1.P8_2, LED1.cathode
  N5: BeagleBone1.P8_13, LED1.anode
  N6: BeagleBone1.P8_19, LED3.anode

custom parts:
  BeagleBone Black: BeagleBone Black rev. C
